# Fritzing sketch sunrise_alarm (saved by Fritzing 0.8.5b)
breadboards: 1

parts:
  part = Arduino Pro Mini v13
  R1 = Resistor [tolerance=±5% resistance=220 package=THT]
  Q1 = Basic FET N-Channel [package="TO220 [THT]"]
  LED_Strip = LEDs [package=led10mm]
  12v_to_5v_Transformer = Transformer [package=transformer]
  IC1 = DS1307 [package=THT]

nets:
  GND: part.GND, R1.Pin_0, Q1.source, IC1.0V
  N1: part.A4, IC1.SCL_-_I2C_Clock
  N2: part.A5, IC1.SDA_-_I2C_Data
  N3: part.VCC, 12v_to_5v_Transformer.4, IC1.+V
  N4: part.A3, R1.Pin_1, Q1.gate
  N5: Q1.drain, LED_Strip.C
  12V: LED_Strip.A, 12v_to_5v_Transformer.1
